# Fritzing sketch OR (saved by Fritzing 1.0.1rc)
breadboards: 1

parts:
  Q1 = NPN-Transistor [package="TO92 [THT]"]
  S1 = Pushbutton [package="[THT]"]
  Q2 = NPN-Transistor [package="TO92 [THT]"]
  S2 = Pushbutton [package="[THT]"]
  LED1 = LED - 5mm [color="Red (633nm)" current=0.030 package="5 mm [THT]"]
  R1 = Resistor [tolerance=±5% power=0.25 resistance=2.2k package=THT]
  R2 = Resistor [tolerance=±5% power=0.25 resistance=2.2k package=THT]
  R3 = Resistor [tolerance=±5% power=0.25 resistance=330 package=THT]
  Power_plug1 = Power plug

nets:
  N1: Q1.E, Q2.E, R1.Pin_0, R2.Pin_0, Power_plug1.GND
  N2: Q1.B, S1.Pin_3, S1.Pin_4
  N3: Q1.C, Q2.C, LED1.cathode
  N4: S1.Pin_1, S1.Pin_2, R1.Pin_1
  N5: Q2.B, S2.Pin_3, S2.Pin_4
  N6: S2.Pin_1, S2.Pin_2, R2.Pin_1
  N7: LED1.anode, R3.Pin_0
  N8: R3.Pin_1, Power_plug1.VCC

notes:
  Compuerta OR
